# Fritzing sketch Untitled Sketch 2 (saved by Fritzing 0.9.3b)

parts:
  WeMos_D1_Mini1 = WeMos D1 Mini
  R1 = PHOTOCELL [package=photocell]
  GY1 = MPU-6050 Board GY-521 [form="♀ (female)" package=THT]
  R2 = Resistor [tolerance=±5% resistance=10k package="1206 [SMD]"]  # not connected

nets:
  N1: WeMos_D1_Mini1.3V3, GY1.pin1
  N2: WeMos_D1_Mini1.A0, R1.P$2
  N3: WeMos_D1_Mini1.D1, GY1.pin3
  N4: WeMos_D1_Mini1.D2, GY1.pin4
  N5: WeMos_D1_Mini1.G, GY1.pin2

custom parts:
  MPU-6050 Board GY-521: Acelerometro y Giroscopio MPU-6050 Board GY-521
